// Digital circuit computer.dig as structural Verilog
module computer (
  input  clk,
  input  Clock_Enable,
  input  [15:0] Data_Bus_Manual_Input,
  input  Manual_Clock_Tick
);

  wire alu_1_p5, ALUn, ALUo, ALUop, ALUre, ALUz, Clock, RAre, RAwr, RBre, RBwr;
  wire [15:0] Register_A_q, Register_B_q;

  assign Clock = ~Clock_Enable ? Manual_Clock_Tick : 1'bz;  // DriverInvSel driverinvsel_1
  assign Clock = Clock_Enable ? clk : 1'bz;  // Driver driver_1
  LED led_1 (.in(Clock_Enable));
  assign Data_Bus_Manual_Input = RAre ? Register_A_q : 16'bz;  // Driver driver_2
  assign Data_Bus_Manual_Input[0] = ALUre ? alu_1_p5 : 1'bz;  // Driver driver_3
  assign Data_Bus_Manual_Input[0] = RBre ? Register_B_q[0] : 1'bz;  // Driver driver_4
  Register #(.Bits(16)) Register_A (.D(Data_Bus_Manual_Input), .C(Clock), .en(RAwr), .Q(Register_A_q));
  Register #(.Bits(16)) Register_B (.D(Data_Bus_Manual_Input), .C(Clock), .en(RBwr), .Q(Register_B_q));
  // ALU alu_1: pin names not known; wires that end beside it: Register_A_q, Register_B_q, ALUop, 1'b0, alu_1_p5, ALUo, ALUz, ALUn
  // Pins of 1 and 16 bits meet at Data_Bus_Manual_Input
  // Pins of 1 and 16 bits meet at Register_B_q
endmodule
